// Logisim project 6651071075_LAB1_BAI1.circ as structural Verilog: 1 circuit, main circuit main
module main (
  input  A2,
  input  A1,
  input  A0,
  input  EN,
  output Y0,
  output Y1,
  output Y2,
  output Y3,
  output Y4,
  output Y5,
  output Y6,
  output Y7
);

  wire nA0, nA1, nA2;

  not not_1 (nA2, A2);
  not not_2 (nA1, A1);
  not not_3 (nA0, A0);
  and and_1 (Y0, EN, nA2, nA1, nA0);
  and and_2 (Y1, EN, nA2, nA1, A0);
  and and_3 (Y2, EN, nA2, A1, nA0);
  and and_4 (Y3, EN, nA2, A1, A0);
  and and_5 (Y4, EN, A2, nA1, nA0);
  and and_6 (Y5, EN, A2, nA1, A0);
  and and_7 (Y6, EN, A2, A1, nA0);
  and and_8 (Y7, EN, A2, A1, A0);
endmodule
